// Digital circuit SLT.dig as structural Verilog
module SLT (
  input  [31:0] rs1,
  input  [31:0] rs2,
  output [31:0] S
);

  Comparator #(.Bits(32)) comparator_1 (.a(rs1), .b(rs2), .lt(S[31]));  // open: gt, eq

  assign S[30:0] = {31{S[31]}};
endmodule
